# Fritzing sketch wiring (saved by Fritzing 0.9.4)
stripboards: 1

parts:
  M1 = DOIT Esp32 DevKit v1 (30 pins long, 11 pins width) [part_number=ESP32S-PIN30]
  KY-1 = Keyes Relay [package=THT]
  KY-2 = Keyes Relay [package=THT]

nets:
  N1: M1.3V3, KY-1.power, KY-2.power
  N2: M1.GND, KY-1.ground, KY-2.ground
  N3: M1.D15, KY-2.signal
  N4: M1.D4, KY-1.signal

notes:
  Fogger Positive
  Fan Positive
  +5V and GND
  Fan PWM

custom parts:
  DOIT Esp32 DevKit v1 (30 pins long, 11 pins width): The DOIT Esp32 DevKit v1 is one of the development board created by DOIT to evaluate the ESP-WROOM-32 module. It is based on the ESP32 microcontroller that boasts Wifi, Bluetooth, Ethernet and Low Power support all in a single chip. (vanepp) made breadboard work, adjusted pin numbering and labels and reduced size of schematic and cleaned up pcb. This chip is 30pins long (2 x15) and 11 pins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
  Keyes Relay: The Keyes 5V relay module is suitable for SCM development, home appliance control. It uses a 5V~12V TIL control signal which can control DC / AC signal.
